# Fritzing sketch snmp_agent_eth01_recovered (saved by Fritzing 1.0.6)
breadboards: 2

parts:
  A1 = wt32-eth01
  Компонент1 = FTDI Basic Programmer
  S1 = Round Pushbutton
  DS1 = DS18B20 1-Wire Temperature Sensor [part_number=DS18B20]
  R1 = Resistor [tolerance=±5% resistance=4.7k package="2512 [SMD]"]
  S2 = Reed switch [package=THT]
  S3 = Reed switch [package=THT]
  Adafruit_Reversible_USB_Type_A_Plug_Connector_Breakout1 = Adafruit Reversible USB Type A Plug Connector Breakout [mn=Adafruit mpn=#6001 part_number=#6001]  # not connected
  JP1 = Header 2 [package=jst-2-pth-kit]  # not connected
  A2 = wt32-eth01
  Компонент2 = FTDI Basic Programmer
  S4 = Pushbutton [package="[THT]"]
  DS2 = DS18B20 1-Wire Temperature Sensor [part_number=DS18B20]
  R2 = Resistor [tolerance=±5% resistance=4.7k package="2512 [SMD]"]  # not connected
  Q1 = PNP-Transistor [package="TO92 [THT]"]
  R3 = Resistor [tolerance=±5% resistance=100k package="2512 [SMD]"]
  R4 = Resistor [tolerance=±5% resistance=1k package="2512 [SMD]"]
  JP2 = Header 2 [package=jst-2-pth-kit]

nets:
  N1: A1.Pin_1, A1.Pin_4
  N2: A1.Pin_2, A1.Pin_9, A1.Pin_11, A1.Pin_14, A1.Pin_23, Компонент1.DTR, S1.leg1, DS1.GND, S3.pin_2
  N3: A1.Pin_3, A1.Pin_10, DS1.DQ, R1.Pin_0
  N4: A1.Pin_5, DS1.VDD, R1.Pin_1
  N5: A1.Pin_12, Компонент1.TXO
  N6: A1.Pin_19, S2.pin_1
  N7: A1.Pin_20, S3.pin_1
  N8: A1.Pin_24, S1.leg0
  N9: A1.Pin_25, Компонент1.POWER
  N10: A1.Pin_26, Компонент1.CTS
  N11: A2.Pin_1, A2.Pin_4
  N12: A2.Pin_2, A2.Pin_9, A2.Pin_11, A2.Pin_14, A2.Pin_23, Компонент2.DTR, S4.Pin_1, S4.Pin_2, DS2.GND, Q1.C, JP2.1
  N13: A2.Pin_3, A2.Pin_10, DS2.DQ, R3.Pin_0
  N14: A2.Pin_5, DS2.VDD
  N15: A2.Pin_6, Q1.B
  N16: A2.Pin_12, Компонент2.TXO
  N17: A2.Pin_24, S4.Pin_3, S4.Pin_4
  N18: A2.Pin_25, Компонент2.POWER
  N19: A2.Pin_26, Компонент2.CTS
  N20: R4.Pin_0, JP2.2

notes:
  это датчик H2O-Контакт (Протечка)
  Это транзистор КТ853Б
  1.База (Б) — левая ножка
  2. Коллектор (К) — средняя ножка
  3. Эмиттер (Э) — правая ножка

custom parts:
  wt32-eth01: WT32-ETH01 is an embedded serial port to Ethernet module based on ESP32 series designed by Wireless-Tag.
